// Logisim project minicomputer.circ as structural Verilog: 4 circuits, main circuit main
module main (
  input  [7:0] in_1
);

  Clock clock_1 ();  // open: out
  D_Flip_Flop d_ff_1 ();  // open: D, clk, Q, Qn, preset, reset
  Register register_1 ();  // open: D, en, clk, Q, clr
  Priority_Encoder priority_encoder_1 ();  // open: in0, in1, in2, in3, in4, in5, in6, in7, out, en_in, gs, en_out
  Multiplexer multiplexer_1 ();  // open: in0, in1, out, sel
  Demultiplexer demultiplexer_1 ();  // open: out0, out1, in, sel
  Decoder decoder_1 ();  // open: out0, out1, sel, en
endmodule

module ALU (
  input  in_1,
  input  in_2,
  input  in_3,
  input  [7:0] D1,
  input  [7:0] D2,
  output [7:0] out_6,
  output [9:0] out_7,
  output out_8,
  output [7:0] out_9,
  output [7:0] out_10,
  output [7:0] out_11,
  output [7:0] out_12,
  output [7:0] out_13,
  output [7:0] out_14
);

  wire full_adder_1_co, full_adder_2_co, full_adder_3_co, full_adder_4_co, full_adder_5_co, full_adder_6_co,
       full_adder_7_co;
  wire [7:0] shifter_1_out;
  wire [8:0] full_adder_1_s;

  full_adder full_adder_1 (.A(D1[0]), .B(D2[0]), .CI(in_1), .CO(full_adder_1_co), .S(full_adder_1_s[0]));
  full_adder full_adder_2 (.A(D1[4]), .B(D2[4]), .CI(full_adder_7_co), .CO(full_adder_2_co), .S(full_adder_1_s[4]));
  full_adder full_adder_3 (.A(D1[1]), .B(D2[1]), .CI(full_adder_1_co), .CO(full_adder_3_co), .S(full_adder_1_s[1]));
  full_adder full_adder_4 (.A(D1[5]), .B(D2[5]), .CI(full_adder_2_co), .CO(full_adder_4_co), .S(full_adder_1_s[5]));
  Subtractor subtractor_1 (.a(D1), .b(D2), .out(out_6), .bin(in_3), .bout(out_8));
  Multiplier multiplier_1 (.a(D1), .b(D2), .out(out_10), .cin(out_9), .cout(out_11));
  Divider divider_1 (.a(D1), .b(D2), .out(out_13), .upper(out_12), .rem(out_14));
  Shifter shifter_1 (.in(D1), .\dist (D2[2:0]), .out(shifter_1_out));
  full_adder full_adder_5 (.A(D1[2]), .B(D2[2]), .CI(full_adder_3_co), .CO(full_adder_5_co), .S(full_adder_1_s[2]));
  full_adder full_adder_6 (.A(D1[6]), .B(D2[6]), .CI(full_adder_4_co), .CO(full_adder_6_co), .S(full_adder_1_s[6]));
  full_adder full_adder_7 (.A(D1[3]), .B(D2[3]), .CI(full_adder_5_co), .CO(full_adder_7_co), .S(full_adder_1_s[3]));
  full_adder full_adder_8 (.A(D1[7]), .B(D2[7]), .CI(full_adder_6_co), .CO(full_adder_1_s[8]), .S(full_adder_1_s[7]));
  Multiplexer #(.select(3), .width(10)) multiplexer_1 (
    .in0({in_2, full_adder_1_s}), .in4({shifter_1_out, {2{in_2}}}), .out(out_7));  // open: in1, in2, in3, in5, in6, in7, sel
endmodule

module full_adder (
  input  A,
  input  B,
  input  CI,
  output CO,
  output S
);

  wire half_adder_1_c, half_adder_1_s, half_adder_2_c;

  half_adder half_adder_1 (.A(A), .B(B), .C(half_adder_1_c), .S(half_adder_1_s));
  half_adder half_adder_2 (.A(half_adder_1_s), .B(CI), .C(half_adder_2_c), .S(S));
  or or_1 (CO, half_adder_1_c, half_adder_2_c);
endmodule

module half_adder (
  input  A,
  input  B,
  output C,
  output S
);

  and and_1 (C, A, B);
  xor xor_1 (S, A, B);
endmodule
